# Fritzing sketch sinereal (saved by Fritzing 0.9.6b)
breadboards: 1

parts:
  LM1 = LM741 [part_number=LM741 package="DIP (Dual Inline) [THT]"]
  R1 = Resistor [tolerance=±5% power=0.25 resistance=10k package=THT]
  RF = Resistor [tolerance=±5% power=0pW resistance=20k package=THT]
  R = Rotary Potentiometer (Small) [maximum_resistance=100kΩ package=THT]
  C = Ceramic Capacitor [capacitance=50pF voltage=35V package="100 mil [THT, multilayer]"]
  C_2 = Ceramic Capacitor [capacitance=50nF voltage=35V package="100 mil [THT, multilayer]"]
  R2 = Rotary Potentiometer (Small) [maximum_resistance=100kΩ package=THT]
  U1 = DIODE-ZENER [package=diode-zener]
  U2 = DIODE-ZENER [package=diode-zener]

nets:
  N1: LM1.pin2, R1.Pin_1, RF.Pin_1
  N2: LM1.pin3, R.leg2, C.1
  -12V: LM1.pin4
  OUTPUT: LM1.pin6
  12V: LM1.pin7
  GND: R1.Pin_0, R.wiper
  N3: RF.Pin_0, C_2.0
  N4: R.leg1, C.0
  N5: C_2.1, R2.leg2
  N6: U1.C, U2.C

custom parts:
  LM741: This is a single Op Amp DIP.
