# Fritzing sketch squarereal (saved by Fritzing 0.9.6b)
breadboards: 1

parts:
  LM1 = LM741 [part_number=LM741 package="DIP (Dual Inline) [THT]"]
  R2 = Resistor [tolerance=±5% power=0.25 resistance=100k package=THT]
  R3 = Resistor [tolerance=±5% power=0.25 resistance=100k package=THT]
  R4 = Resistor [tolerance=±5% power=0.25 resistance=10k package=THT]
  C = Ceramic Capacitor [capacitance=47nF voltage=35V package="100 mil [THT, multilayer]"]
  R5 = Resistor [tolerance=±5% power=0.25 resistance=10k package=THT]
  R = Rotary Potentiometer (Small) [maximum_resistance=100kΩ package=THT]
  U1 = DIODE-ZENER [package=diode-zener]
  U2 = DIODE-ZENER [package=diode-zener]

nets:
  N1: LM1.pin2, R3.Pin_1
  -12V: LM1.pin4
  OUTPUT: LM1.pin6, R4.Pin_1, R.leg2, U1.A
  12V: LM1.pin7
  N2: R2.Pin_0, R4.Pin_0, R5.Pin_0
  N3: R3.Pin_0, C.1, R.leg1
  GND: C.0, R5.Pin_1, R.wiper, U2.A
  N4: U1.C, U2.C

custom parts:
  LM741: This is a single Op Amp DIP.
