# Fritzing sketch trianglereal (saved by Fritzing 0.9.6b)
breadboards: 1

parts:
  LM1 = LM741 [part_number=LM741 package="DIP (Dual Inline) [THT]"]
  R2 = Resistor [tolerance=±5% power=0.25 resistance=100k package=THT]
  R3 = Resistor [tolerance=±5% power=0.25 resistance=100k package=THT]
  R4 = Resistor [tolerance=±5% power=0.25 resistance=10k package=THT]
  C = Ceramic Capacitor [capacitance=47nF voltage=35V package="100 mil [THT, multilayer]"]
  R5 = Resistor [tolerance=±5% power=0.25 resistance=10k package=THT]
  R = Rotary Potentiometer (Small) [maximum_resistance=100kΩ package=THT]
  U1 = DIODE-ZENER [package=diode-zener]
  U2 = DIODE-ZENER [package=diode-zener]
  LM2 = LM741 [part_number=LM741 package="DIP (Dual Inline) [THT]"]
  R6 = Resistor [tolerance=±5% power=0.25 resistance=100k package=THT]
  C1 = Ceramic Capacitor [capacitance=50nF voltage=35V package="100 mil [THT, multilayer]"]
  R7 = Resistor [tolerance=±5% power=0.25 resistance=10k package=THT]
  U3 = DIODE-ZENER [package=diode-zener]
  U4 = DIODE-ZENER [package=diode-zener]
  R8 = Resistor [tolerance=±5% power=0.25 resistance=10k package=THT]

nets:
  N1: LM1.pin2, R3.Pin_1
  -12V: LM1.pin4, LM2.pin4
  N2: LM1.pin6, R4.Pin_1, R.leg2, R6.Pin_0
  12V: LM1.pin7, LM2.pin7
  N3: R2.Pin_0, R4.Pin_0, R5.Pin_0
  N4: R3.Pin_0, C.1, R.leg1
  GND: C.0, R5.Pin_1, R.wiper, U2.A, U3.A, R8.Pin_1
  N5: U1.C, U2.C
  N6: LM2.pin2, R8.Pin_0
  N7: LM2.pin3, R6.Pin_1
  OUTPUT: LM2.pin6, C1.1, R7.Pin_1, U4.A
  N8: C1.0, R7.Pin_0
  N9: U3.C, U4.C

custom parts:
  LM741: This is a single Op Amp DIP.
